# Fritzing sketch EXPLORATION CIRCUIT DESIGN (saved by Fritzing 0.8.7b)

parts:
  Part4 = Arduino Mega ADK (Rev3)
  OLED_I2C2 = OLED 128x64 I2C Monochrome Display
  S3 = Round Pushbutton
  S4 = Round Pushbutton
  Part5 = EasyDriver_v44  # not connected
  Part6 = EasyDriver_v44
  M3 = Stepper Motor - Bipolar  # not connected
  M4 = Stepper Motor - Bipolar  # not connected

nets:
  N1: Part4.A15, OLED_I2C2.SDA
  N2: Part4.D13_PWM, S3.leg1
  N3: Part4.D12_PWM, S4.leg1
  GND: Part4.GND, OLED_I2C2.GND, Part6.GND
  N4: Part4.VIN, Part6.V+
  N5: S3.leg0, S4.leg0
